// Logisim project MIPS.circ as structural Verilog: 9 circuits, main circuit main
// MemWrite
module main (
  output RegDest,
  output ALUSrc,
  output MemToReg,
  output RegWrite,
  output MemRead,
  output MemWrite,
  output Branch,
  output Jump,
  output AluOP1,
  output AluOP0,
  output [5:0] Opcode_R,
  output [4:0] Rs,
  output [4:0] Rt,
  output [4:0] Rd,
  output [4:0] Shamt,
  output [31:0] Operando1,
  output [5:0] Funct,
  output [5:0] Opcode_J,
  output [31:0] Operando2,
  output [25:0] Target,
  output [5:0] Opcode_I,
  output Zero,
  output [4:0] Rs_2,
  output [4:0] Rt_2,
  output [31:0] Result,
  output [15:0] Immediate,
  output [23:0] Branch_Dir,
  output [31:0] ALU_Result,
  output [31:0] Write_Data,
  output Branch_2,
  output Zero_2,
  output RegWrite_2,
  output MemWrite_2,
  output MemToReg_2,
  output [4:0] RegWriteAddr
);

  wire and_1_out, button_2_out, clk, reset;
  wire [2:0] alu_control_1_out_4;
  wire [4:0] led_1_esp1, led_1_esp2, led_1_esp3, led_1_esp4, led_1_exit1_l1, led_1_exit1_l2, led_1_exit1_l3,
       led_1_exit1_l4, led_1_exit2_l1, led_1_exit2_l2, led_1_exit2_l3, led_1_exit2_l4, led_1_exit3_l1,
       led_1_exit3_l2, led_1_exit3_l3, led_1_exit3_l4, multiplexer_1_out, multiplexer_2_out;
  wire [23:0] adder_2_out, adder_3_out, bit_extender_1_out, bit_extender_3_out, multiplexer_4_out, PC,
       returnPC, shifter_1_out, sumout;
  wire [31:0] bit_extender_2_out, INSTR, multiplexer_3_out;

  Clock clock_1 (.out(clk));
  Register_part #(.width(24)) u_PC (.D(returnPC), .Q(PC), .clk(clk), .clr(reset));  // open: en
  Button button_1 (.out(reset));
  Adder #(.width(24)) adder_1 (.a(24'h1), .b(PC), .out(sumout));  // open: cin, cout
  Button button_2 (.out(button_2_out));
  RAM #(.addrWidth(24), .dataWidth(32)) ram_1 (
    .addr(PC), .data(INSTR), .clk(clk), .clr(button_2_out));  // open: sel, ld
  ID id_1 (
    .\input (INSTR), .Opcode_R(Opcode_R), .Rd(Rd), .Rt(Rt), .Rs(Rs), .Funct(Funct), .Shamt(Shamt),
    .target(Target), .Immediate(Immediate), .Opcode_J(Opcode_J), .Rt_2(Rt_2), .Rs_2(Rs_2), .Opcode_I(Opcode_I));
  Adder #(.width(24)) adder_2 (.a(PC), .b(bit_extender_1_out), .out(adder_2_out));  // open: cin, cout
  assign bit_extender_1_out = {{8{1'b0}}, Immediate};  // Bit_Extender bit_extender_1
  Multiplexer #(.width(5), .enable("false")) multiplexer_1 (.in0(Rt), .in1(Rd), .out(multiplexer_1_out), .sel(RegDest));
  DotMatrix #(.matrixcols(16), .matrixrows(5)) dotmatrix_1 (
    .col0(led_1_exit1_l1), .col1(led_1_exit2_l1), .col2(led_1_exit3_l1), .col3(led_1_esp1),
    .col4(led_1_exit1_l2), .col5(led_1_exit2_l2), .col6(led_1_exit3_l2), .col7(led_1_esp2),
    .col8(led_1_exit1_l3), .col9(led_1_exit2_l3), .col10(led_1_exit3_l3), .col11(led_1_esp4),
    .col12(led_1_exit1_l4), .col13(led_1_exit2_l4), .col14(led_1_exit3_l4), .col15(led_1_esp3));
  LED led_1 (
    .input_clk(clk), .type_funct(INSTR[5:0]), .offcode(INSTR[31:26]), .ESP2(led_1_esp2), .ESP1(led_1_esp1),
    .ESP3(led_1_esp3), .ESP4(led_1_esp4), .Exit1_L1(led_1_exit1_l1), .Exit2_L1(led_1_exit2_l1),
    .Exit3_L1(led_1_exit3_l1), .Exit1_L2(led_1_exit1_l2), .Exit2_L2(led_1_exit2_l2),
    .Exit3_L2(led_1_exit3_l2), .Exit1_L3(led_1_exit1_l3), .Exit2_L3(led_1_exit2_l3),
    .Exit3_L3(led_1_exit3_l3), .Exit1_L4(led_1_exit1_l4), .Exit2_L4(led_1_exit2_l4), .Exit3_L4(led_1_exit3_l4));
  Data_Mem data_mem_1 (
    .Branch_Dir(adder_2_out), .ALU_Result(Result), .Write_Data(Operando2), .branch(Branch), .Zero(Zero),
    .RegWrite(RegWrite), .MemWrite(MemWrite), .MemToReg(MemToReg), .RegWriteAdrs(multiplexer_1_out),
    .Clock(clk), .out_11(Branch_Dir), .out_12(ALU_Result), .out_13(Write_Data), .out_14(Branch_2),
    .out_15(Zero_2), .out_16(RegWrite_2), .out_17(MemWrite_2), .out_18(MemToReg_2), .out_19(RegWriteAddr));
  Control control_1 (
    .Instruction(INSTR), .RegDst(RegDest), .ALUSrc(ALUSrc), .MemToReg(MemToReg), .RegWrite(RegWrite),
    .MemRead(MemRead), .MemWrite(MemWrite), .Branch(Branch), .Jump(Jump), .ALUOp1(AluOP1), .ALUOp0(AluOP0));
  Multiplexer #(.width(5)) multiplexer_2 (
    .in0(INSTR[20:16]), .in1(INSTR[15:11]), .out(multiplexer_2_out), .sel(RegDest));  // open: en
  // Probe on Result
  Register register_1 (
    .Clock(clk), .Reg_Write(RegWrite), .Rs(INSTR[25:21]), .Rt(INSTR[20:16]), .Rd(multiplexer_2_out),
    .Write(Result), .Out1(Operando1), .Out2(Operando2));
  assign bit_extender_2_out = {{16{1'b0}}, Immediate};  // Bit_Extender bit_extender_2
  Multiplexer #(.width(32)) multiplexer_3 (
    .in0(Operando2), .in1(bit_extender_2_out), .out(multiplexer_3_out), .sel(ALUSrc));  // open: en
  // Probe on alu_control_1_out_4
  ALU_Control alu_control_1 (.aluop0(AluOP0), .aluop1(AluOP1), .Funct(INSTR[5:0]), .out_4(alu_control_1_out_4));
  ALU alu_1 (
    .Operand1(Operando1), .Operand2(multiplexer_3_out), .ALU_Op(alu_control_1_out_4), .Zero(Zero),
    .ALU_Result(Result));
  assign bit_extender_3_out = {{8{1'b0}}, Immediate};  // Bit_Extender bit_extender_3
  Shifter #(.width(24)) shifter_1 (.in(bit_extender_3_out), .\dist (5'b00010), .out(shifter_1_out));
  // Probe on shifter_1_out
  Adder #(.width(24)) adder_3 (.a(sumout), .b(shifter_1_out), .out(adder_3_out));  // open: cin, cout
  Multiplexer #(.width(24), .enable("false")) multiplexer_4 (
    .in0(sumout), .in1(adder_3_out), .out(multiplexer_4_out), .sel(and_1_out));
  and and_1 (and_1_out, Branch, Zero);
  Multiplexer #(.width(24), .enable("false")) multiplexer_5 (
    .in0(multiplexer_4_out), .in1(INSTR[23:0]), .out(returnPC), .sel(Jump));
  Multiplexer multiplexer_6 ();  // open: in0, in1, out, sel, en

  // Other names for the same wires on the sheet: ALU_Result_t[31:0] = Result; Imm[15:0] = Immediate;
  //   Operand1[31:0] = Operando1; Operand2[31:0] = Operando2
endmodule

// Instruction Decoder
module ID (
  input  [31:0] \input ,
  output [5:0] Funct,
  output [4:0] Shamt,
  output [4:0] Rd,
  output [4:0] Rt,
  output [4:0] Rs,
  output [5:0] Opcode_R,
  output [25:0] target,
  output [5:0] Opcode_J,
  output [15:0] Immediate,
  output [4:0] Rt_2,
  output [4:0] Rs_2,
  output [5:0] Opcode_I
);


  assign Funct = \input [5:0];
  assign Immediate = \input [15:0];
  assign Opcode_I = \input [31:26];
  assign Opcode_J = \input [31:26];
  assign Opcode_R = \input [31:26];
  assign Rd = \input [15:11];
  assign Rs = \input [25:21];
  assign Rs_2 = \input [25:21];
  assign Rt = \input [20:16];
  assign Rt_2 = \input [20:16];
  assign Shamt = \input [10:6];
  assign target = \input [25:0];
endmodule

module LED (
  input  input_clk,
  input  [5:0] type_funct,
  input  [5:0] offcode,
  output [4:0] ESP2,
  output [4:0] ESP1,
  output [4:0] ESP3,
  output [4:0] ESP4,
  output [4:0] Exit1_L1,
  output [4:0] Exit2_L1,
  output [4:0] Exit3_L1,
  output [4:0] Exit1_L2,
  output [4:0] Exit2_L2,
  output [4:0] Exit3_L2,
  output [4:0] Exit1_L3,
  output [4:0] Exit2_L3,
  output [4:0] Exit3_L3,
  output [4:0] Exit1_L4,
  output [4:0] Exit2_L4,
  output [4:0] Exit3_L4
);

  wire and_1_out, and_2_out, and_3_out, and_4_out, and_5_out, and_6_out, and_7_out, and_8_out, clock,
       comparator_1_eq, comparator_2_eq, comparator_3_eq, comparator_3_gt, comparator_3_lt, comparator_4_eq,
       comparator_5_eq, comparator_6_eq, comparator_7_eq, comparator_8_eq, not_2_out, not_3_out, not_4_out,
       not_5_out, not_6_out, not_7_out, not_8_out, or_1_out, or_2_out;
  wire [2:0] or_3_out, register_1_q, register_2_q, register_3_q, register_4_q, register_5_q, register_6_q,
       register_7_q;
  wire [15:15] rom_1_data, rom_2_data, rom_3_data, rom_4_data;

  Comparator #(.width(6)) comparator_1 (.a(6'b100000), .b(type_funct), .eq(comparator_1_eq));  // open: gt, lt
  Comparator #(.width(6)) comparator_2 (.a(type_funct), .b(6'b100010), .eq(comparator_2_eq));  // open: gt, lt
  Comparator #(.width(6)) comparator_3 (
    .a(offcode), .b({6{1'b0}}), .gt(comparator_3_gt), .eq(comparator_3_eq), .lt(comparator_3_lt));
  or or_1 (or_1_out, comparator_3_gt, comparator_3_lt);
  Comparator #(.width(6)) comparator_4 (.a(offcode), .b(6'b001000), .eq(comparator_4_eq));  // open: gt, lt
  Comparator #(.width(6)) comparator_5 (.a(offcode), .b(6'b100011), .eq(comparator_5_eq));  // open: gt, lt
  Comparator #(.width(6)) comparator_6 (.a(6'b101011), .b(offcode), .eq(comparator_6_eq));  // open: gt, lt
  Comparator #(.width(6)) comparator_7 (.a(6'b000100), .b(offcode), .eq(comparator_7_eq));  // open: gt, lt
  Comparator #(.width(6)) comparator_8 (.a(6'b000010), .b(offcode), .eq(comparator_8_eq));  // open: gt, lt
  and and_1 (and_1_out, comparator_1_eq, comparator_3_eq);
  and and_2 (and_2_out, comparator_2_eq, comparator_3_eq);
  and and_3 (and_3_out, or_1_out, comparator_4_eq);
  and and_4 (and_4_out, or_1_out, comparator_5_eq);
  and and_5 (and_5_out, or_1_out, comparator_6_eq);
  and and_6 (and_6_out, or_1_out, comparator_7_eq);
  and and_7 (and_7_out, or_1_out, comparator_8_eq);
  not not_1 (clock, input_clk);
  not not_2 (not_2_out, and_2_out);
  not not_3 (not_3_out, and_3_out);
  not not_4 (not_4_out, and_4_out);
  not not_5 (not_5_out, and_5_out);
  not not_6 (not_6_out, and_6_out);
  not not_7 (not_7_out, and_7_out);
  or or_2 (or_2_out, and_4_out, and_5_out);
  Register_part #(.width(3)) register_1 (.D(3'b001), .en(and_1_out), .Q(register_1_q), .clk(clock), .clr(not_8_out));
  not not_8 (not_8_out, and_1_out);
  Register_part #(.width(3)) register_2 (.D(3'b010), .en(and_2_out), .Q(register_2_q), .clk(clock), .clr(not_2_out));
  Register_part #(.width(3)) register_3 (.D(3'b011), .en(and_3_out), .Q(register_3_q), .clk(clock), .clr(not_3_out));
  Register_part #(.width(3)) register_4 (.D(3'b100), .en(and_4_out), .Q(register_4_q), .clk(clock), .clr(not_4_out));
  Register_part #(.width(3)) register_5 (.D(3'b101), .en(and_5_out), .Q(register_5_q), .clk(clock), .clr(not_5_out));
  Register_part #(.width(3)) register_6 (.D(3'b110), .en(and_6_out), .Q(register_6_q), .clk(clock), .clr(not_6_out));
  Register_part #(.width(3)) register_7 (.D(3'b111), .en(and_7_out), .Q(register_7_q), .clk(clock), .clr(not_7_out));
  and and_8 (and_8_out, 1'b1, or_2_out);
  Multiplexer #(.width(5)) multiplexer_1 (.in0({5{1'b0}}), .in1(5'b00001), .out(ESP2), .sel(and_8_out), .en(1'b1));
  assign or_3_out = register_1_q | register_2_q | register_3_q | register_4_q | register_5_q | register_6_q | register_7_q;  // OR_Gate or_3, 3 bits wide
  // Probe on or_3_out
  ROM #(.addrWidth(3), .dataWidth(16)) rom_1 (
    .addr(or_3_out), .data({rom_1_data[15], Exit1_L1, Exit2_L1, Exit3_L1}));  // open: sel
  ROM #(.addrWidth(3), .dataWidth(16)) rom_2 (
    .addr(or_3_out), .data({rom_2_data[15], Exit1_L2, Exit2_L2, Exit3_L2}));  // open: sel
  ROM #(.addrWidth(3), .dataWidth(16)) rom_3 (
    .addr(or_3_out), .data({rom_3_data[15], Exit1_L3, Exit2_L3, Exit3_L3}));  // open: sel
  ROM #(.addrWidth(3), .dataWidth(16)) rom_4 (
    .addr(or_3_out), .data({rom_4_data[15], Exit1_L4, Exit2_L4, Exit3_L4}));  // open: sel

  assign ESP1 = {5{1'b0}};
  assign ESP3 = {5{1'b0}};
  assign ESP4 = {5{1'b0}};

  // Notes on the sheet:
  //   Add
  //   sub
  //   addi
  //   ld
  //   sw
  //   Beq
  //   J
  //   contents of rom_1 (hex, n*v repeats v):
  //   0 7e9f 76b7 7e9f 7c21 76b7 7ca7 47f0
  //   contents of rom_2 (hex, n*v repeats v):
  //   0 7e2e 7c3f 7e2e 7827 7827 7eb1
  //   contents of rom_3 (hex, n*v repeats v):
  //   0 7e2e 7ca7 7e2e 7800 7800 729f
  //   contents of rom_4 (hex, n*v repeats v):
  //   0 0 0 47f1
endmodule

module Control (
  input  [31:0] Instruction,
  output RegDst,
  output ALUSrc,
  output MemToReg,
  output RegWrite,
  output MemRead,
  output MemWrite,
  output Branch,
  output Jump,
  output ALUOp1,
  output ALUOp0
);

  wire and_2_out, and_3_out, not_1_out, not_2_out, not_3_out, not_4_out, not_5_out, not_6_out, not_7_out,
       not_8_out, not_9_out, not_10_out;

  not not_1 (not_1_out, Instruction[29]);
  and and_1 (RegDst, not_1_out, not_2_out);
  not not_2 (not_2_out, Instruction[27]);
  or or_1 (ALUSrc, Instruction[27], Instruction[29]);
  not not_3 (not_3_out, Instruction[28]);
  and and_2 (and_2_out, not_3_out, not_4_out);
  not not_4 (not_4_out, Instruction[27]);
  and and_3 (and_3_out, Instruction[31], not_5_out);
  not not_5 (not_5_out, Instruction[29]);
  and and_4 (MemRead, Instruction[31], not_6_out);
  not not_6 (not_6_out, Instruction[29]);
  and and_5 (MemWrite, Instruction[31], Instruction[29]);
  and and_6 (Jump, Instruction[27], not_7_out);
  not not_7 (not_7_out, Instruction[26]);
  not not_8 (not_8_out, Instruction[29]);
  and and_7 (ALUOp1, not_8_out, not_9_out, not_10_out);
  not not_9 (not_9_out, Instruction[28]);
  not not_10 (not_10_out, Instruction[27]);
  or or_2 (RegWrite, and_2_out, and_3_out);

  assign ALUOp0 = Instruction[28];
  assign Branch = Instruction[28];
  assign MemToReg = Instruction[27];
endmodule

module Register (
  input  Clock,
  input  Reg_Write,
  input  [4:0] Rs,
  input  [4:0] Rt,
  input  [4:0] Rd,
  input  [31:0] Write,
  output [31:0] Out1,
  output [31:0] Out2
);

  wire clk, demultiplexer_2_out20, demultiplexer_2_out21, demultiplexer_2_out22, demultiplexer_2_out23,
       demultiplexer_2_out24, demultiplexer_2_out25, demultiplexer_2_out26, demultiplexer_2_out27,
       demultiplexer_2_out28, demultiplexer_2_out29, demultiplexer_2_out30, demultiplexer_2_out31, e0, e1,
       e2, e3, e4, e5, e6, e7, e8, e9, e10, e11, e12, e13, e14, e15;
  wire [31:0] demultiplexer_1_out0, demultiplexer_1_out1, demultiplexer_1_out2, demultiplexer_1_out3,
       demultiplexer_1_out4, demultiplexer_1_out5, demultiplexer_1_out6, demultiplexer_1_out7,
       demultiplexer_1_out8, demultiplexer_1_out9, demultiplexer_1_out10, demultiplexer_1_out11,
       demultiplexer_1_out12, demultiplexer_1_out13, demultiplexer_1_out14, demultiplexer_1_out15,
       demultiplexer_1_out16, demultiplexer_1_out17, demultiplexer_1_out18, demultiplexer_1_out19,
       demultiplexer_1_out20, demultiplexer_1_out21, demultiplexer_1_out22, demultiplexer_1_out23,
       demultiplexer_1_out24, demultiplexer_1_out25, demultiplexer_1_out26, demultiplexer_1_out27,
       demultiplexer_1_out28, demultiplexer_1_out29, demultiplexer_1_out30, demultiplexer_1_out31, R0, R1,
       R2, R3, R4, R5, R6, R7, R8, R9, R10, R11, R12, R13, R14, R15, R16, R17, R18, R19, R20, R21, R22, R23,
       R24, R25, R26, R27, R28, R29, R30, R31;

  not not_1 (clk, Clock);
  Demultiplexer #(.select(5), .width(32), .enable("false")) demultiplexer_1 (
    .out0(demultiplexer_1_out0), .out1(demultiplexer_1_out1), .out2(demultiplexer_1_out2),
    .out3(demultiplexer_1_out3), .out4(demultiplexer_1_out4), .out5(demultiplexer_1_out5),
    .out6(demultiplexer_1_out6), .out7(demultiplexer_1_out7), .out8(demultiplexer_1_out8),
    .out9(demultiplexer_1_out9), .out10(demultiplexer_1_out10), .out11(demultiplexer_1_out11),
    .out12(demultiplexer_1_out12), .out13(demultiplexer_1_out13), .out14(demultiplexer_1_out14),
    .out15(demultiplexer_1_out15), .out16(demultiplexer_1_out16), .out17(demultiplexer_1_out17),
    .out18(demultiplexer_1_out18), .out19(demultiplexer_1_out19), .out20(demultiplexer_1_out20),
    .out21(demultiplexer_1_out21), .out22(demultiplexer_1_out22), .out23(demultiplexer_1_out23),
    .out24(demultiplexer_1_out24), .out25(demultiplexer_1_out25), .out26(demultiplexer_1_out26),
    .out27(demultiplexer_1_out27), .out28(demultiplexer_1_out28), .out29(demultiplexer_1_out29),
    .out30(demultiplexer_1_out30), .out31(demultiplexer_1_out31), .in(Write), .sel(Rd));
  Demultiplexer #(.select(5), .enable("false")) demultiplexer_2 (
    .out0(e0), .out1(e1), .out2(e2), .out3(e3), .out4(e4), .out5(e5), .out6(e6), .out7(e7), .out8(e8),
    .out9(e9), .out10(e10), .out11(e11), .out12(e12), .out13(e13), .out14(e14), .out15(e15), .out16(e15),
    .out17(e15), .out18(e15), .out19(e15), .out20(demultiplexer_2_out20), .out21(demultiplexer_2_out21),
    .out22(demultiplexer_2_out22), .out23(demultiplexer_2_out23), .out24(demultiplexer_2_out24),
    .out25(demultiplexer_2_out25), .out26(demultiplexer_2_out26), .out27(demultiplexer_2_out27),
    .out28(demultiplexer_2_out28), .out29(demultiplexer_2_out29), .out30(demultiplexer_2_out30),
    .out31(demultiplexer_2_out31), .in(Reg_Write), .sel(Rd));
  Multiplexer #(.select(5), .width(32), .enable("false")) multiplexer_1 (
    .in0(R0), .in1(R1), .in2(R2), .in3(R3), .in4(R4), .in5(R5), .in6(R26), .in7(R7), .in8(R8), .in9(R9),
    .in10(R10), .in11(R11), .in12(R12), .in13(R13), .in14(R14), .in15(R15), .in16(R16), .in17(R17),
    .in18(R18), .in19(R19), .in20(R20), .in21(R21), .in22(R22), .in23(R23), .in24(R24), .in25(R25),
    .in26(R26), .in27(R27), .in28(R28), .in29(R29), .in30(R30), .in31(R31), .out(Out1), .sel(Rs));
  Register_part #(.width(32)) register_1 (.D(demultiplexer_1_out0), .en(e0), .Q(R0), .clk(clk));  // open: clr
  Register_part #(.width(32)) register_2 (.D(demultiplexer_1_out16), .en(e15), .Q(R16), .clk(clk));  // open: clr
  Register_part #(.width(32)) register_3 (.D(demultiplexer_1_out1), .en(e1), .Q(R1), .clk(clk));  // open: clr
  Register_part #(.width(32)) register_4 (.D(demultiplexer_1_out17), .en(e15), .Q(R17), .clk(clk));  // open: clr
  Register_part #(.width(32)) register_5 (.D(demultiplexer_1_out2), .en(e2), .Q(R2), .clk(clk));  // open: clr
  Register_part #(.width(32)) register_6 (.D(demultiplexer_1_out18), .en(e15), .Q(R18), .clk(clk));  // open: clr
  Register_part #(.width(32)) register_7 (.D(demultiplexer_1_out3), .en(e3), .Q(R3), .clk(clk));  // open: clr
  Register_part #(.width(32)) register_8 (.D(demultiplexer_1_out19), .en(e15), .Q(R19), .clk(clk));  // open: clr
  Register_part #(.width(32)) register_9 (.D(demultiplexer_1_out4), .en(e4), .Q(R4), .clk(clk));  // open: clr
  Register_part #(.width(32)) register_10 (
    .D(demultiplexer_1_out20), .en(demultiplexer_2_out20), .Q(R20), .clk(clk));  // open: clr
  Register_part #(.width(32)) register_11 (.D(demultiplexer_1_out5), .en(e5), .Q(R5), .clk(clk));  // open: clr
  Register_part #(.width(32)) register_12 (
    .D(demultiplexer_1_out21), .en(demultiplexer_2_out21), .Q(R21), .clk(clk));  // open: clr
  // Probe on Rt
  Register_part #(.width(32)) register_13 (.D(demultiplexer_1_out6), .en(e6), .Q(R6), .clk(clk));  // open: clr
  Register_part #(.width(32)) register_14 (
    .D(demultiplexer_1_out22), .en(demultiplexer_2_out22), .Q(R22), .clk(clk));  // open: clr
  Register_part #(.width(32)) register_15 (.D(demultiplexer_1_out7), .en(e7), .Q(R7), .clk(clk));  // open: clr
  Register_part #(.width(32)) register_16 (
    .D(demultiplexer_1_out23), .en(demultiplexer_2_out23), .Q(R23), .clk(clk));  // open: clr
  Multiplexer #(.select(5), .width(32), .enable("false")) multiplexer_2 (
    .in0(R0), .in1(R1), .in2(R2), .in3(R3), .in4(R4), .in5(R5), .in6(R26), .in7(R7), .in8(R8), .in9(R9),
    .in10(R10), .in11(R11), .in12(R12), .in13(R13), .in14(R14), .in15(R15), .in16(R16), .in17(R17),
    .in18(R18), .in19(R19), .in20(R20), .in21(R21), .in22(R22), .in23(R23), .in24(R24), .in25(R25),
    .in26(R26), .in27(R27), .in28(R28), .in29(R29), .in30(R30), .in31(R31), .out(Out2), .sel(Rt));
  Register_part #(.width(32)) register_17 (.D(demultiplexer_1_out8), .en(e8), .Q(R8), .clk(clk));  // open: clr
  Register_part #(.width(32)) register_18 (
    .D(demultiplexer_1_out24), .en(demultiplexer_2_out24), .Q(R24), .clk(clk));  // open: clr
  Register_part #(.width(32)) register_19 (.D(demultiplexer_1_out9), .en(e9), .Q(R9), .clk(clk));  // open: clr
  Register_part #(.width(32)) register_20 (
    .D(demultiplexer_1_out25), .en(demultiplexer_2_out25), .Q(R25), .clk(clk));  // open: clr
  Register_part #(.width(32)) register_21 (.D(demultiplexer_1_out10), .en(e10), .Q(R10), .clk(clk));  // open: clr
  Register_part #(.width(32)) register_22 (
    .D(demultiplexer_1_out26), .en(demultiplexer_2_out26), .Q(R26), .clk(clk));  // open: clr
  Register_part #(.width(32)) register_23 (.D(demultiplexer_1_out11), .en(e11), .Q(R11), .clk(clk));  // open: clr
  Register_part #(.width(32)) register_24 (
    .D(demultiplexer_1_out27), .en(demultiplexer_2_out27), .Q(R27), .clk(clk));  // open: clr
  Register_part #(.width(32)) register_25 (.D(demultiplexer_1_out12), .en(e12), .Q(R12), .clk(clk));  // open: clr
  Register_part #(.width(32)) register_26 (
    .D(demultiplexer_1_out28), .en(demultiplexer_2_out28), .Q(R28), .clk(clk));  // open: clr
  Register_part #(.width(32)) register_27 (.D(demultiplexer_1_out13), .en(e13), .Q(R13), .clk(clk));  // open: clr
  Register_part #(.width(32)) register_28 (
    .D(demultiplexer_1_out29), .en(demultiplexer_2_out29), .Q(R29), .clk(clk));  // open: clr
  Register_part #(.width(32)) register_29 (.D(demultiplexer_1_out14), .en(e14), .Q(R14), .clk(clk));  // open: clr
  Register_part #(.width(32)) register_30 (
    .D(demultiplexer_1_out30), .en(demultiplexer_2_out30), .Q(R30), .clk(clk));  // open: clr
  Register_part #(.width(32)) register_31 (.D(demultiplexer_1_out15), .en(e15), .Q(R15), .clk(clk));  // open: clr
  Register_part #(.width(32)) register_32 (
    .D(demultiplexer_1_out31), .en(demultiplexer_2_out31), .Q(R31), .clk(clk));  // open: clr

  // Other names for the same wires on the sheet: RegWrite = Reg_Write
endmodule

module ALU_Control (
  input  aluop0,
  input  aluop1,
  input  [5:0] Funct,
  output [2:0] out_4
);

  wire comparator_1_lt;
  wire [1:0] or_1_out;
  wire [2:2] and_1_out;

  // Probe on {aluop1, aluop0}
  and and_1 (and_1_out[2], 1'b1, aluop1);
  not not_1 (or_1_out[1], Funct[2]);
  or or_1 (or_1_out[0], Funct[0], Funct[3]);
  // Probe on {and_1_out[2], 2'b10}
  // Probe on {Funct[1], or_1_out}
  // Probe on {aluop1, aluop0}
  Comparator #(.width(2), .mode("unsigned")) comparator_1 (
    .a(2'b01), .b({aluop1, aluop0}), .lt(comparator_1_lt));  // open: gt, eq
  Multiplexer #(.width(3)) multiplexer_1 (
    .in0({and_1_out[2], 2'b10}), .in1({Funct[1], or_1_out}), .out(out_4), .sel(comparator_1_lt));  // open: en

  // Other names for the same wires on the sheet: opun[1:0] = {aluop1, aluop0}
endmodule

module ALU (
  input  [31:0] Operand1,
  input  [31:0] Operand2,
  input  [2:0] ALU_Op,
  output Zero,
  output [31:0] ALU_Result
);

  wire [31:0] adder_1_out, and_1_out, multiplier_1_out, or_1_out, subtractor_1_out;

  Comparator #(.width(32)) comparator_1 (.a(Operand1), .b(Operand2), .eq(Zero));  // open: gt, lt
  Adder #(.width(32)) adder_1 (.a(Operand1), .b(Operand2), .out(adder_1_out));  // open: cin, cout
  Subtractor #(.width(32)) subtractor_1 (.a(Operand1), .b(Operand2), .out(subtractor_1_out));  // open: bin, bout
  Multiplier #(.width(32)) multiplier_1 (.a(Operand1), .b(Operand2), .out(multiplier_1_out));  // open: cin, cout
  Divider #(.width(32)) divider_1 (.a(Operand1), .b(Operand2));  // open: out, upper, rem
  assign and_1_out = Operand1 & Operand2;  // AND_Gate and_1, 32 bits wide
  assign or_1_out = Operand1 | Operand2;  // OR_Gate or_1, 32 bits wide
  // XOR_Gate xor_1 has open pins: in0=Operand1, in1=Operand2, out=open
  Multiplexer #(.select(3), .width(32), .enable("false")) multiplexer_1 (
    .in0(and_1_out), .in1(or_1_out), .in2(adder_1_out), .in4(multiplier_1_out), .in6(subtractor_1_out),
    .in7({32{1'b0}}), .out(ALU_Result), .sel(ALU_Op));  // open: in3, in5
endmodule

// Data Memory
module Data_Mem (
  input  Clock,
  input  [23:0] Branch_Dir,
  input  [31:0] ALU_Result,
  input  [31:0] Write_Data,
  input  branch,
  input  Zero,
  input  RegWrite,
  input  MemWrite,
  input  MemToReg,
  input  [4:0] RegWriteAdrs,
  output [23:0] out_11,
  output [31:0] out_12,
  output [31:0] out_13,
  output out_14,
  output out_15,
  output out_16,
  output out_17,
  output out_18,
  output [4:0] out_19
);

  Register_part #(.width(24)) register_1 (.D(Branch_Dir), .en(1'b1), .Q(out_11), .clk(Clock));  // open: clr
  Register_part #(.width(32)) register_2 (.D(ALU_Result), .en(1'b1), .Q(out_12), .clk(Clock));  // open: clr
  Register_part #(.width(32)) register_3 (.D(Write_Data), .en(1'b1), .Q(out_13), .clk(Clock));  // open: clr
  Register_part #(.width(1)) register_4 (.D(branch), .en(1'b1), .Q(out_14), .clk(Clock));  // open: clr
  Register_part #(.width(1)) register_5 (.D(Zero), .en(1'b1), .Q(out_15), .clk(Clock));  // open: clr
  Register_part #(.width(1)) register_6 (.D(RegWrite), .en(1'b1), .Q(out_16), .clk(Clock));  // open: clr
  Register_part #(.width(1)) register_7 (.D(MemWrite), .en(1'b1), .Q(out_17), .clk(Clock));  // open: clr
  Register_part #(.width(1)) register_8 (.D(MemToReg), .en(1'b1), .Q(out_18), .clk(Clock));  // open: clr
  Register_part #(.width(5)) register_9 (.D(RegWriteAdrs), .en(1'b1), .Q(out_19), .clk(Clock));  // open: clr
endmodule

module Control_Combinacional (
  input  op5,
  input  op4,
  input  op3,
  input  op2,
  input  op1,
  input  op0,
  output RegDst,
  output ALUSrc,
  output MemToReg,
  output RegWrite,
  output MemRead,
  output MemWrite,
  output Branch,
  output Jump,
  output ALUOp1,
  output ALUOp0
);

  wire and_3_out, and_4_out, not_1_out, not_2_out, not_3_out, not_4_out, not_5_out, not_6_out, not_7_out,
       not_8_out, not_9_out, not_10_out;

  not not_1 (not_1_out, op3);
  not not_2 (not_2_out, op1);
  or or_1 (ALUSrc, op1, op3);
  not not_3 (not_3_out, op2);
  not not_4 (not_4_out, op1);
  not not_5 (not_5_out, op3);
  not not_6 (not_6_out, op3);
  and and_1 (MemWrite, op5, op3);
  not not_7 (not_7_out, op0);
  not not_8 (not_8_out, op3);
  not not_9 (not_9_out, op2);
  not not_10 (not_10_out, op1);
  and and_2 (RegDst, not_1_out, not_2_out);
  and and_3 (and_3_out, not_3_out, not_4_out);
  and and_4 (and_4_out, op5, not_5_out);
  and and_5 (MemRead, op5, not_6_out);
  and and_6 (Jump, op1, not_7_out);
  and and_7 (ALUOp1, not_8_out, not_9_out, not_10_out);
  or or_2 (RegWrite, and_3_out, and_4_out);

  assign ALUOp0 = op2;
  assign Branch = op2;
  assign MemToReg = op1;
endmodule
